// Digital circuit cpu.dig as structural Verilog
module cpu (
  input  clk,
  input  [6:0] in_4,
  input  [31:0] in_5,
  input  [31:0] in_6,
  input  [31:0] in_7,
  input  [31:0] in_8,
  input  [31:0] in_9,
  input  [31:0] in_10,
  input  [2:0] in_11,
  output [31:0] out_2,
  output [31:0] out_3
);

  wire button_1_out, u_Control_Uint_ex_en, u_Control_Uint_expc_en, u_Control_Uint_id_en,
       u_Control_Uint_imm_en, u_Control_Uint_jump_en, u_Control_Uint_l_or_s, u_Control_Uint_mem_en,
       u_Control_Uint_pc_en, u_Control_Uint_wb_en;
  wire [1:0] u_Control_Uint_wb_ctrl;

  Button #(.activeLow("true")) button_1 (.out(button_1_out));
  Control_Uint #(.applicationType("IVERILOG"), .CodeFile("D:\\CPU\\design\\Control_Unit.v")) u_Control_Uint (
    .clk(clk), .rst(button_1_out), .ALUSEL(in_4), .PC_en(u_Control_Uint_pc_en), .ID_en(u_Control_Uint_id_en),
    .EX_en(u_Control_Uint_ex_en), .MEM_en(u_Control_Uint_mem_en), .WB_en(u_Control_Uint_wb_en),
    .Jump_en(u_Control_Uint_jump_en), .imm_en(u_Control_Uint_imm_en), .EXPC_en(u_Control_Uint_expc_en),
    .L_or_S(u_Control_Uint_l_or_s), .WB_Ctrl(u_Control_Uint_wb_ctrl));
  LED led_1 (.in(u_Control_Uint_pc_en));
  LED led_2 (.in(u_Control_Uint_id_en));
  LED led_3 (.in(u_Control_Uint_mem_en));
  LED led_4 (.in(u_Control_Uint_wb_en));
  LED led_5 (.in(u_Control_Uint_jump_en));
  LED led_6 (.in(u_Control_Uint_l_or_s));
  ex #(.applicationType("IVERILOG"), .CodeFile("D:\\CPU\\design\\ex.v")) u_ex (
    .rst(button_1_out), .en(u_Control_Uint_ex_en), .pc_en(u_Control_Uint_expc_en),
    .imm_en(u_Control_Uint_imm_en), .pc(in_7), .reg_1(in_8), .reg_2(in_9), .imm(in_10), .aluop(in_11),
    .alu_result(out_2));
  WB #(.applicationType("IVERILOG"), .CodeFile("D:\\CPU\\design\\WB.v")) u_WB (
    .RAM_Data(in_5), .PC_Plus4(in_6), .EX_Data(out_2), .WB_Ctrl(u_Control_Uint_wb_ctrl), .WB_Data(out_3));

  // Notes on the sheet:
  //   clk: Hz: 2
  //   in_7: default 1
  //   in_8: default 70
  //   in_9: default 6
  //   in_10: default 4
  //   in_11: default 3
endmodule
